// Digital circuit 4bit.Processor.dlogic.dig as structural Verilog
module _4bit_Processor_dlogic (
  input  Load,
  input  Clock,
  input  [3:0] Data,
  input  [3:0] Input,
  input  [2:0] Control,
  input  [3:0] Placeholder,
  input  Cin,
  output zero_flag,
  output Cout,
  output SLT,
  output [3:0] Output
);

  wire cpucontrolunit_1_immediate_load, cpucontrolunit_1_read_register_1, cpucontrolunit_1_read_register_2,
       cpucontrolunit_1_write_register;
  wire [3:0] _4bit_ir_1_p3, _4bit_memorymodule_1_output, _4bit_programcounter_1_p5,
       _4bit_registerfile_1_read_data_1, _4bit_registerfile_1_read_data_2, multiplexer_1_out;

  // _4bit_ProgramCounter _4bit_programcounter_1: pin names not known; wires that end beside it: Input, Load, 1'b1, Clock, _4bit_programcounter_1_p5
  _4bit_MemoryModule _4bit_memorymodule_1 (
    .Data(Data), .Write_Address(_4bit_programcounter_1_p5), .Read_Input(_4bit_programcounter_1_p5),
    .Clock(Clock), .Output(_4bit_memorymodule_1_output));
  // _4bit_IR _4bit_ir_1: pin names not known; wires that end beside it: _4bit_memorymodule_1_output, Clock, _4bit_ir_1_p3
  CPUControlUnit cpucontrolunit_1 (
    .IR(_4bit_ir_1_p3), .Read_Register_1(cpucontrolunit_1_read_register_1),
    .Read_Register_2(cpucontrolunit_1_read_register_2), .Write_Register(cpucontrolunit_1_write_register),
    .Immediate_Load(cpucontrolunit_1_immediate_load));  // open: Write_Enable
  _4bit_RegisterFile _4bit_registerfile_1 (
    .Read_register_1(cpucontrolunit_1_read_register_1), .Read_register_2(cpucontrolunit_1_read_register_2),
    .write_register(cpucontrolunit_1_write_register), .Write_data(multiplexer_1_out), .Clock(Clock),
    .Read_data_1(_4bit_registerfile_1_read_data_1), .Read_data_2(_4bit_registerfile_1_read_data_2));
  // _4bit_ALU_Sana__2 _4bit_alu_sana__2_1: pin names not known; wires that end beside it: _4bit_registerfile_1_read_data_1, _4bit_registerfile_1_read_data_2, Control, Cin, Placeholder, Placeholder, Output, zero_flag, Cout, SLT
  Multiplexer #(.Bits(4)) multiplexer_1 (
    .sel(cpucontrolunit_1_immediate_load), .in_0(Output), .in_1(_4bit_memorymodule_1_output),
    .out(multiplexer_1_out));
endmodule
