// Digital circuit 4bit_CPU.dlogic.ProgramCounter.dig as structural Verilog
module _4bit_CPU_dlogic_ProgramCounter (
  input  [3:0] in_1,
  input  Load,
  input  Increment,
  input  clk,
  output [3:0] out_5
);

  wire and_1_out;
  wire [3:0] add_1_s, multiplexer_1_out;

  D_FF d_ff_1 (.D(multiplexer_1_out[0]), .C(clk), .Q(out_5[0]));  // open: nQ
  D_FF d_ff_2 (.D(multiplexer_1_out[1]), .C(clk), .Q(out_5[1]));  // open: nQ
  D_FF d_ff_3 (.D(multiplexer_1_out[2]), .C(clk), .Q(out_5[2]));  // open: nQ
  D_FF d_ff_4 (.D(multiplexer_1_out[3]), .C(clk), .Q(out_5[3]));  // open: nQ
  and and_1 (and_1_out, Load, Increment);
  Multiplexer #(.Bits(4)) multiplexer_1 (.sel(and_1_out), .in_0(add_1_s), .in_1(in_1), .out(multiplexer_1_out));
  Add #(.Bits(4)) add_1 (.a(out_5), .b(4'b0001), .c_i(1'b0), .s(add_1_s));  // open: c_o
endmodule
