// Digital circuit 4bit_IR.dig as structural Verilog
module _4bit_IR (
  input  [3:0] in_2,
  input  clk,
  output [3:0] Output
);

  D_FF d_ff_1 (.D(in_2[0]), .C(clk), .Q(Output[0]));  // open: nQ
  D_FF d_ff_2 (.D(in_2[1]), .C(clk), .Q(Output[1]));  // open: nQ
  D_FF d_ff_3 (.D(in_2[2]), .C(clk), .Q(Output[2]));  // open: nQ
  D_FF d_ff_4 (.D(in_2[3]), .C(clk), .Q(Output[3]));  // open: nQ
endmodule
