// Digital circuit 4bit_MemoryModule.dig as structural Verilog
module _4bit_MemoryModule (
  input  [3:0] Data,
  input  [3:0] Write,
  input  Clock,
  input  [3:0] Read,
  output [3:0] Output
);

  wire [3:0] _4bit_register_1_p1, _4bit_register_1_p3, _4bit_register_2_p1, _4bit_register_2_p3,
       _4bit_register_3_p1, _4bit_register_3_p3, _4bit_register_4_p1, _4bit_register_4_p3,
       _4bit_register_5_p1, _4bit_register_5_p3, _4bit_register_6_p1, _4bit_register_6_p3,
       _4bit_register_7_p1, _4bit_register_7_p3, _4bit_register_8_p1, _4bit_register_8_p3,
       _4bit_register_9_p1, _4bit_register_9_p3, _4bit_register_10_p1, _4bit_register_10_p3,
       _4bit_register_11_p1, _4bit_register_11_p3, _4bit_register_12_p1, _4bit_register_12_p3,
       _4bit_register_13_p1, _4bit_register_13_p3, _4bit_register_14_p1, _4bit_register_14_p3,
       _4bit_register_15_output, _4bit_register_16_p1, _4bit_register_16_p3;

  Multiplexer #(.Bits(4), .Selector_Bits(4)) multiplexer_1 (
    .sel(Write), .in_1(_4bit_register_16_p1), .in_2(_4bit_register_14_p1), .in_3(_4bit_register_13_p1),
    .in_4(_4bit_register_12_p1), .in_5(_4bit_register_11_p1), .in_6(_4bit_register_10_p1),
    .in_7(_4bit_register_9_p1), .in_8(_4bit_register_8_p1), .in_9(_4bit_register_7_p1),
    .in_10(_4bit_register_6_p1), .in_11(_4bit_register_5_p1), .in_12(_4bit_register_4_p1),
    .in_13(_4bit_register_3_p1), .in_14(_4bit_register_2_p1), .in_15(_4bit_register_1_p1), .out(Data));  // open: in_0
  // _4bit_Register _4bit_register_1: pin names not known; wires that end beside it: _4bit_register_1_p1, Clock, _4bit_register_1_p3
  // _4bit_Register _4bit_register_2: pin names not known; wires that end beside it: _4bit_register_2_p1, Clock, _4bit_register_2_p3
  // _4bit_Register _4bit_register_3: pin names not known; wires that end beside it: _4bit_register_3_p1, Clock, _4bit_register_3_p3
  // _4bit_Register _4bit_register_4: pin names not known; wires that end beside it: _4bit_register_4_p1, Clock, _4bit_register_4_p3
  // _4bit_Register _4bit_register_5: pin names not known; wires that end beside it: _4bit_register_5_p1, Clock, _4bit_register_5_p3
  // _4bit_Register _4bit_register_6: pin names not known; wires that end beside it: _4bit_register_6_p1, Clock, _4bit_register_6_p3
  // _4bit_Register _4bit_register_7: pin names not known; wires that end beside it: _4bit_register_7_p1, Clock, _4bit_register_7_p3
  // _4bit_Register _4bit_register_8: pin names not known; wires that end beside it: _4bit_register_8_p1, Clock, _4bit_register_8_p3
  // _4bit_Register _4bit_register_9: pin names not known; wires that end beside it: _4bit_register_9_p1, Clock, _4bit_register_9_p3
  // _4bit_Register _4bit_register_10: pin names not known; wires that end beside it: _4bit_register_10_p1, Clock, _4bit_register_10_p3
  // _4bit_Register _4bit_register_11: pin names not known; wires that end beside it: _4bit_register_11_p1, Clock, _4bit_register_11_p3
  // _4bit_Register _4bit_register_12: pin names not known; wires that end beside it: _4bit_register_12_p1, Clock, _4bit_register_12_p3
  // _4bit_Register _4bit_register_13: pin names not known; wires that end beside it: _4bit_register_13_p1, Clock, _4bit_register_13_p3
  // _4bit_Register _4bit_register_14: pin names not known; wires that end beside it: _4bit_register_14_p1, Clock, _4bit_register_14_p3
  _4bit_Register _4bit_register_15 (.clk(Clock), .Output(_4bit_register_15_output));  // open: input
  // _4bit_Register _4bit_register_16: pin names not known; wires that end beside it: _4bit_register_16_p1, Clock, _4bit_register_16_p3
  Multiplexer #(.Bits(4), .Selector_Bits(4)) multiplexer_2 (
    .sel(Read), .in_0(_4bit_register_1_p3), .in_1(_4bit_register_2_p3), .in_2(_4bit_register_3_p3),
    .in_3(_4bit_register_4_p3), .in_4(_4bit_register_5_p3), .in_5(_4bit_register_6_p3),
    .in_6(_4bit_register_7_p3), .in_7(_4bit_register_8_p3), .in_8(_4bit_register_9_p3),
    .in_9(_4bit_register_10_p3), .in_10(_4bit_register_11_p3), .in_11(_4bit_register_12_p3),
    .in_12(_4bit_register_13_p3), .in_13(_4bit_register_14_p3), .in_14(_4bit_register_15_output),
    .in_15(_4bit_register_16_p3), .out(Output));
endmodule
