// Digital circuit 4bit_Register.dig as structural Verilog
module _4bit_Register (
  input  [1:0] in_1,
  input  [3:0] \input ,
  input  clk,
  output [3:0] Output
);

  wire [3:0] multiplexer_1_out;

  Multiplexer #(.Bits(4), .Selector_Bits(2)) multiplexer_1 (
    .sel(in_1), .in_0(Output), .in_1(\input ), .in_2(4'b0000), .in_3(4'b0000),
    .out({{2{multiplexer_1_out[3]}}, multiplexer_1_out[1:0]}));
  D_FF d_ff_1 (.D(multiplexer_1_out[0]), .C(clk), .Q(Output[0]));  // open: nQ
  D_FF d_ff_2 (.D(multiplexer_1_out[1]), .C(clk), .Q(Output[1]));  // open: nQ
  D_FF d_ff_3 (.D(multiplexer_1_out[3]), .C(clk), .Q(Output[2]));  // open: nQ
  D_FF d_ff_4 (.D(multiplexer_1_out[3]), .C(clk), .Q(Output[3]));  // open: nQ
endmodule
