// Digital circuit 4bit_RegisterFile.dig as structural Verilog
module _4bit_RegisterFile (
  input  [1:0] Read_register_1,
  input  [1:0] Read_register_2,
  input  [1:0] write_register,
  input  [3:0] Write_data,
  input  Clock,
  output [3:0] Read_data_1,
  output [3:0] Read_data_2
);

  wire [3:0] demultiplexer_1_out_0, demultiplexer_1_out_1, demultiplexer_1_out_2, demultiplexer_1_out_3,
       register_cpu_1_output, register_cpu_2_output, register_cpu_3_output, register_cpu_4_output;

  Demultiplexer #(.Selector_Bits(2), .Bits(4)) demultiplexer_1 (
    .sel(write_register), .in(Write_data), .out_0(demultiplexer_1_out_0), .out_1(demultiplexer_1_out_1),
    .out_2(demultiplexer_1_out_2), .out_3(demultiplexer_1_out_3));
  Register_CPU register_cpu_1 (.Input(demultiplexer_1_out_3), .Clock(Clock), .Output(register_cpu_1_output));
  Register_CPU register_cpu_2 (.Input(demultiplexer_1_out_0), .Clock(Clock), .Output(register_cpu_2_output));
  Register_CPU register_cpu_3 (.Input(demultiplexer_1_out_1), .Clock(Clock), .Output(register_cpu_3_output));
  Register_CPU register_cpu_4 (.Input(demultiplexer_1_out_2), .Clock(Clock), .Output(register_cpu_4_output));
  Multiplexer #(.Selector_Bits(2), .Bits(4)) multiplexer_1 (
    .sel(Read_register_1), .in_0(register_cpu_2_output), .in_1(register_cpu_3_output),
    .in_2(register_cpu_4_output), .in_3(register_cpu_1_output), .out(Read_data_1));
  Multiplexer #(.Selector_Bits(2), .Bits(4)) multiplexer_2 (
    .sel(Read_register_2), .in_0(register_cpu_2_output), .in_1(register_cpu_3_output),
    .in_2(register_cpu_4_output), .in_3(register_cpu_1_output), .out(Read_data_2));
endmodule
