// Digital circuit CPUControlUnit.dig as structural Verilog
module CPUControlUnit (
  input  [3:0] IR,
  output Read_Register_1,
  output Read_Register_2,
  output Write_Register,
  output Write_Enable,
  output Immediate_Load
);

  wire and_1_out, and_2_out, and_3_out, and_4_out, not_1_out, not_2_out, not_3_out, not_4_out, not_5_out,
       not_6_out, not_7_out, not_8_out, not_9_out;

  not not_1 (not_1_out, IR[0]);
  not not_2 (not_2_out, IR[2]);
  not not_3 (not_3_out, IR[0]);
  not not_4 (not_4_out, IR[2]);
  not not_5 (not_5_out, IR[0]);
  not not_6 (not_6_out, IR[1]);
  not not_7 (not_7_out, IR[2]);
  not not_8 (not_8_out, IR[0]);
  not not_9 (not_9_out, IR[1]);
  and and_1 (and_1_out, not_1_out, IR[1], not_2_out);
  and and_2 (and_2_out, not_3_out, IR[1], not_4_out);
  and and_3 (and_3_out, not_5_out, not_6_out, not_7_out);
  and and_4 (and_4_out, not_8_out, not_9_out, IR[2]);
  or or_1 (Read_Register_1, and_1_out, and_2_out);
  or or_2 (Immediate_Load, and_3_out, and_4_out);

  assign Read_Register_2 = Read_Register_1;
  assign Write_Enable = Immediate_Load;
  assign Write_Register = Read_Register_1;
endmodule
