// Digital circuit ControlUnit.dig as structural Verilog
module ControlUnit (
  input  [3:0] IR,
  output [3:0] ALU_operation_selec,
  output [3:0] Read_Register_1,
  output [3:0] Read_Register_2,
  output [3:0] Write_Register,
  output [3:0] Immediate_Load
);

  wire [3:0] decoder_1_out_0, decoder_1_out_1, decoder_1_out_2, decoder_1_out_3, decoder_1_out_4,
       decoder_1_out_5, decoder_1_out_6, decoder_1_out_7, decoder_1_out_8, decoder_1_out_9, decoder_1_out_10,
       decoder_1_out_11, decoder_1_out_12, decoder_1_out_13, decoder_1_out_14, decoder_1_out_15, not_1_out,
       not_2_out, not_3_out, not_4_out, not_5_out, not_6_out, not_7_out, not_8_out, not_9_out, not_10_out,
       not_11_out;

  Decoder #(.Selector_Bits(4)) decoder_1 (
    .sel(IR), .out_0(decoder_1_out_0[0]), .out_1(decoder_1_out_1[0]), .out_2(decoder_1_out_2[0]),
    .out_3(decoder_1_out_3[0]), .out_4(decoder_1_out_4[0]), .out_5(decoder_1_out_5[0]),
    .out_6(decoder_1_out_6[0]), .out_7(decoder_1_out_7[0]), .out_8(decoder_1_out_8[0]),
    .out_9(decoder_1_out_9[0]), .out_10(decoder_1_out_10[0]), .out_11(decoder_1_out_11[0]),
    .out_12(decoder_1_out_12[0]), .out_13(decoder_1_out_13[0]), .out_14(decoder_1_out_14[0]),
    .out_15(decoder_1_out_15[0]));
  assign not_1_out = ~decoder_1_out_0;  // Not not_1, 4 bits wide
  assign not_2_out = ~decoder_1_out_1;  // Not not_2, 4 bits wide
  assign not_3_out = ~decoder_1_out_2;  // Not not_3, 4 bits wide
  assign not_4_out = ~decoder_1_out_3;  // Not not_4, 4 bits wide
  assign not_5_out = ~decoder_1_out_4;  // Not not_5, 4 bits wide
  assign not_6_out = ~decoder_1_out_5;  // Not not_6, 4 bits wide
  assign not_7_out = ~decoder_1_out_6;  // Not not_7, 4 bits wide
  assign not_8_out = ~decoder_1_out_7;  // Not not_8, 4 bits wide
  assign not_9_out = ~decoder_1_out_8;  // Not not_9, 4 bits wide
  assign not_10_out = ~decoder_1_out_9;  // Not not_10, 4 bits wide
  assign not_11_out = ~decoder_1_out_10;  // Not not_11, 4 bits wide
  assign ALU_operation_selec = not_1_out | not_2_out | not_3_out | not_4_out | not_5_out | not_6_out | not_7_out | not_8_out | not_9_out | not_10_out | not_11_out | decoder_1_out_11 | decoder_1_out_12 | decoder_1_out_13 | decoder_1_out_14 | decoder_1_out_15;  // Or or_1, 4 bits wide
  // Pins of 1 and 4 bits meet at decoder_1_out_0
  // Pins of 1 and 4 bits meet at decoder_1_out_1
  // Pins of 1 and 4 bits meet at decoder_1_out_2
  // Pins of 1 and 4 bits meet at decoder_1_out_3
  // Pins of 1 and 4 bits meet at decoder_1_out_4
  // Pins of 1 and 4 bits meet at decoder_1_out_5
  // Pins of 1 and 4 bits meet at decoder_1_out_6
  // Pins of 1 and 4 bits meet at decoder_1_out_7
  // Pins of 1 and 4 bits meet at decoder_1_out_8
  // Pins of 1 and 4 bits meet at decoder_1_out_9
  // Pins of 1 and 4 bits meet at decoder_1_out_10
  // Pins of 1 and 4 bits meet at decoder_1_out_11

  assign Immediate_Load = ALU_operation_selec;
  assign Read_Register_1 = ALU_operation_selec;
  assign Read_Register_2 = ALU_operation_selec;
  assign Write_Register = ALU_operation_selec;
endmodule
