// Digital circuit FetchDecodeExceute.dig as structural Verilog
module FetchDecodeExceute (
  input  Input_A,
  input  Input_B,
  input  Clock
);

  wire and_1_out, and_2_out, d_ff_1_q, d_ff_2_q, not_1_out, not_2_out, or_1_out;

  not not_1 (not_1_out, Input_A);
  not not_2 (not_2_out, Input_B);
  and and_1 (and_1_out, not_1_out, Input_A);
  and and_2 (and_2_out, not_2_out, Input_B);
  or or_1 (or_1_out, d_ff_1_q, and_1_out, and_2_out, d_ff_2_q);
  D_FF d_ff_1 (.D(or_1_out), .C(Clock), .Q(d_ff_1_q));  // open: nQ
  D_FF d_ff_2 (.D(or_1_out), .C(Clock), .Q(d_ff_2_q));  // open: nQ
endmodule
