// Digital circuit InstructionDecoder.dig as structural Verilog
module InstructionDecoder (
  input  Register_1,
  input  Register_2,
  input  [2:0] Opcode,
  output Write_Register,
  output [3:0] Write_Enable,
  output [3:0] Immediate_Load,
  output [3:0] ALU_operation_select
);

  wire and_1_out, and_2_out, decoder_1_out_0, decoder_1_out_1, decoder_1_out_2, decoder_1_out_3,
       decoder_1_out_4, decoder_1_out_5, decoder_1_out_6, decoder_1_out_7, not_1_out, not_2_out, not_3_out,
       or_1_out;

  Multiplexer multiplexer_1 (.sel(or_1_out), .in_0(Register_1), .in_1(Register_2), .out(Write_Register));
  or or_1 (or_1_out, Register_1, Register_2);
  Decoder #(.Selector_Bits(3)) decoder_1 (
    .sel(Opcode), .out_0(decoder_1_out_0), .out_1(decoder_1_out_1), .out_2(decoder_1_out_2),
    .out_3(decoder_1_out_3), .out_4(decoder_1_out_4), .out_5(decoder_1_out_5), .out_6(decoder_1_out_6),
    .out_7(decoder_1_out_7));
  not not_1 (not_1_out, decoder_1_out_0);
  not not_2 (not_2_out, decoder_1_out_1);
  not not_3 (not_3_out, decoder_1_out_2);
  and and_1 (and_1_out, not_1_out, not_2_out, not_3_out, decoder_1_out_3);
  and and_2 (and_2_out, decoder_1_out_4, decoder_1_out_5, decoder_1_out_6, decoder_1_out_7);
  or or_2 (ALU_operation_select[0], and_1_out, and_2_out);
  // Pins of 1 and 4 bits meet at ALU_operation_select

  assign Immediate_Load = ALU_operation_select;
  assign Write_Enable = ALU_operation_select;
endmodule
