// Digital circuit Register_CPU.dig as structural Verilog
module Register_CPU (
  input  [3:0] Input,
  input  Clock,
  output [3:0] Output
);

  D_FF d_ff_1 (.D(Input[0]), .C(Clock), .Q(Output[0]));  // open: nQ
  D_FF d_ff_2 (.D(Input[1]), .C(Clock), .Q(Output[1]));  // open: nQ
  D_FF d_ff_3 (.D(Input[2]), .C(Clock), .Q(Output[2]));  // open: nQ
  D_FF d_ff_4 (.D(Input[3]), .C(Clock), .Q(Output[3]));  // open: nQ
endmodule
